# Fritzing sketch Layout (saved by Fritzing 0.8.7b)
breadboards: 1

parts:
  Bauteil1 = Arduino Nano (Rev3.0)
  S1 = Round Pushbutton  # not connected
  U2 = 7-SEGMENT-4DIGIT [package=7-segment-4digit_longpads_for_pogobed]

nets:
  N1: Bauteil1.A7, U2.1
